// Digital circuit Control.dig as structural Verilog
module Control (
  input  Zero,
  input  [6:0] OPCode,
  input  [2:0] Funct3,
  input  [6:0] Funct7,
  input  [31:0] ALU_out,
  output [1:0] ResultSrc,
  output [1:0] PCSrc,
  output MemWrite,
  output [2:0] ALUControl,
  output ALUSrc,
  output [1:0] IMMSrc,
  output RegWrite,
  output HALT
);

  wire Funct7Control, not_1_out, not_2_out, xor_1_out;
  wire [0:0] and_2_out, and_3_out;
  wire [1:0] multiplexer_2_out, rom_1_d;
  wire [1:1] and_1_out;
  wire [3:3] rom_1_d_3;
  wire [11:0] rom_1_d_2;

  not not_1 (not_1_out, ALU_out[0]);
  ROM #(.AddrBits(7), .Bits(13)) rom_1 (
    .A(OPCode), .sel(1'b1),
    .D({Funct7Control, HALT, RegWrite, IMMSrc, ALUSrc, MemWrite, ResultSrc, rom_1_d_3[3], rom_1_d_2[1:0], rom_1_d[1]}));
  not not_2 (not_2_out, Zero);
  Multiplexer #(.Bits(7)) multiplexer_1 (.sel(Funct7Control), .in_0({7{1'b0}}), .in_1(Funct7), .out(rom_1_d_2[11:5]));
  and and_1 (and_1_out[1], rom_1_d[1], rom_1_d_3[3]);
  or or_1 (rom_1_d[0], not_1_out, Zero);
  and and_2 (and_2_out[0], not_2_out, rom_1_d_3[3]);
  and and_3 (and_3_out[0], Zero, rom_1_d_3[3]);
  ROM #(.AddrBits(12), .Bits(3)) rom_2 (.A({rom_1_d_2[11:5], Funct3, rom_1_d_2[1:0]}), .sel(1'b1), .D(ALUControl));
  Multiplexer #(.Selector_Bits(2), .Bits(2)) multiplexer_2 (
    .sel({Funct3[2], Funct3[0]}), .in_0({rom_1_d[1], and_3_out[0]}), .in_1({rom_1_d[1], and_2_out[0]}),
    .in_2({rom_1_d[1], ALU_out[0]}), .in_3(rom_1_d), .out(multiplexer_2_out));
  xor xor_1 (xor_1_out, rom_1_d[1], rom_1_d_3[3]);
  Multiplexer #(.Bits(2)) multiplexer_3 (
    .sel(xor_1_out), .in_0({2{and_1_out[1]}}), .in_1(multiplexer_2_out), .out(PCSrc));

  // Other names for the same wires on the sheet: Seletor[1:0] = {Funct3[2], Funct3[0]}

  // Notes on the sheet:
  //   contents of rom_1 (hex, n*v repeats v):
  //   0,800,0,490,15*0,484,15*0,1c0,15*0,1404,47*0,20a,0,0,0,4af,7*0,721
  //   contents of rom_2 (hex, n*v repeats v):
  //   0,1,0,0,0,1,5,0,0,0,6,6*0,6,2,0,0,6,4*0,3,0,0,0,4,995*0,1
endmodule
