// Digital circuit Extend.dig as structural Verilog
module Extend (
  input  [31:0] I_T,
  input  [31:0] S_T,
  input  [31:0] B_T,
  input  [31:0] J_T,
  input  [1:0] IMMSre,
  output [31:0] S
);

  wire [31:0] bitextender_1_out, bitextender_2_out, bitextender_3_out, bitextender_4_out;

  BitExtender #(.inputBits(12), .outputBits(32)) bitextender_1 (.in({S_T[31:25], S_T[11:7]}), .out(bitextender_1_out));
  BitExtender #(.inputBits(21), .outputBits(32)) bitextender_2 (
    .in({J_T[31], J_T[19:12], J_T[20], J_T[30:21], 1'b0}), .out(bitextender_2_out));
  BitExtender #(.inputBits(12), .outputBits(32)) bitextender_3 (.in(I_T[31:20]), .out(bitextender_3_out));
  BitExtender #(.inputBits(13), .outputBits(32)) bitextender_4 (
    .in({B_T[31], B_T[7], B_T[30:25], B_T[11:8], 1'b0}), .out(bitextender_4_out));
  Multiplexer #(.Bits(32), .Selector_Bits(2)) multiplexer_1 (
    .sel(IMMSre), .in_0(bitextender_3_out), .in_1(bitextender_1_out), .in_2(bitextender_4_out),
    .in_3(bitextender_2_out), .out(S));
endmodule
