// Digital circuit FA1.dig as structural Verilog
module FA1 (
  input  A,
  input  B,
  input  Cin,
  output Cout,
  output S
);

  wire and_1_out, and_2_out, or_1_out;

  and and_1 (and_1_out, A, B);
  or or_1 (or_1_out, A, B);
  and and_2 (and_2_out, Cin, or_1_out);
  xor xor_1 (S, Cin, A, B);
  or or_2 (Cout, and_1_out, and_2_out);
endmodule
