// Digital circuit FA16.dig as structural Verilog
module FA16 (
  input  Cin,
  input  [15:0] A,
  input  [15:0] B,
  output Cout,
  output [15:0] S
);

  wire fa4_1_cout, fa4_2_cout, fa4_3_cout;

  FA4 fa4_1 (.Cin(Cin), .A(A[3:0]), .B(B[3:0]), .Cout(fa4_1_cout), .S(S[3:0]));
  FA4 fa4_2 (.Cin(fa4_1_cout), .A(A[7:4]), .B(B[7:4]), .Cout(fa4_2_cout), .S(S[7:4]));
  FA4 fa4_3 (.Cin(fa4_2_cout), .A(A[11:8]), .B(B[11:8]), .Cout(fa4_3_cout), .S(S[11:8]));
  FA4 fa4_4 (.Cin(fa4_3_cout), .A(A[15:12]), .B(B[15:12]), .Cout(Cout), .S(S[15:12]));
endmodule
