// Digital circuit FA32.dig as structural Verilog
module FA32 (
  input  [31:0] rs2,
  input  [31:0] rs1,
  input  Cin,
  output Cout,
  output [31:0] S
);

  wire fa16_1_cout;

  FA16 fa16_1 (.Cin(Cin), .A(rs1[15:0]), .B(rs2[15:0]), .Cout(fa16_1_cout), .S(S[15:0]));
  FA16 fa16_2 (.Cin(fa16_1_cout), .A(rs1[31:16]), .B(rs2[31:16]), .Cout(Cout), .S(S[31:16]));
endmodule
