// Digital circuit FA4.dig as structural Verilog
module FA4 (
  input  Cin,
  input  [3:0] A,
  input  [3:0] B,
  output Cout,
  output [3:0] S
);

  wire fa1_1_cout, fa1_2_cout, fa1_3_cout;

  FA1 fa1_1 (.A(A[0]), .B(B[0]), .Cin(Cin), .Cout(fa1_1_cout), .S(S[0]));
  FA1 fa1_2 (.A(A[1]), .B(B[1]), .Cin(fa1_1_cout), .Cout(fa1_2_cout), .S(S[1]));
  FA1 fa1_3 (.A(A[2]), .B(B[2]), .Cin(fa1_2_cout), .Cout(fa1_3_cout), .S(S[2]));
  FA1 fa1_4 (.A(A[3]), .B(B[3]), .Cin(fa1_3_cout), .Cout(Cout), .S(S[3]));
endmodule
