// Digital circuit RISC_V.dig as structural Verilog
module RISC_V (
  input  CLK
);

  wire ALUSrc, HALT, MemWrite, multiplexer_3_out, RegWrite, Zero, zero7_1_s;
  wire [1:0] IMMSrc, PCSrc, ResultSrc;
  wire [2:0] ALUControl;
  wire [31:0] ALU_out, B_T, blockramdualport_1_d, extend_1_s, multiplexer_1_out, multiplexer_2_out,
       multiplexer_4_out, multiplexer_5_out, PC, PC_plus_0, PC_plus_4, rd1, registerfile_1_db;

  Multiplexer #(.Selector_Bits(2), .Bits(32)) multiplexer_1 (
    .sel(PCSrc), .in_0(PC_plus_4), .in_1(PC_plus_0), .in_2(PC_plus_0), .in_3(ALU_out), .out(multiplexer_1_out));
  Multiplexer #(.Bits(32)) multiplexer_2 (
    .sel(HALT), .in_0(multiplexer_1_out), .in_1(PC_plus_0), .out(multiplexer_2_out));
  D_FF #(.Bits(32)) IP (.D(multiplexer_2_out), .C(CLK), .Q(PC));  // open: nQ
  Add #(.Bits(32)) add_1 (.a(PC), .b(32'h4), .c_i(1'b0), .s(PC_plus_4));  // open: c_o
  ROM #(.AddrBits(7), .Bits(32)) Mem__Inst (.A(PC[6:0]), .sel(1'b1), .D(B_T));
  Control control_1 (
    .Zero(Zero), .OPCode(B_T[6:0]), .Funct3(B_T[14:12]), .Funct7(B_T[31:25]), .ALU_out(ALU_out),
    .ResultSrc(ResultSrc), .PCSrc(PCSrc), .MemWrite(MemWrite), .ALUControl(ALUControl), .ALUSrc(ALUSrc),
    .IMMSrc(IMMSrc), .RegWrite(RegWrite), .HALT(HALT));
  Multiplexer multiplexer_3 (.sel(zero7_1_s), .in_0(RegWrite), .in_1(1'b0), .out(multiplexer_3_out));
  ZERO7 zero7_1 (.OP(B_T[11:7]), .S(zero7_1_s));
  RegisterFile #(.AddrBits(5), .Bits(32)) registerfile_1 (
    .Din(multiplexer_5_out), .we(multiplexer_3_out), .Rw(B_T[11:7]), .C(CLK), .Ra(B_T[19:15]),
    .Rb(B_T[24:20]), .Da(rd1), .Db(registerfile_1_db));
  Extend extend_1 (.I_T(B_T), .S_T(B_T), .B_T(B_T), .J_T(B_T), .IMMSre(IMMSrc), .S(extend_1_s));
  Multiplexer #(.Bits(32)) multiplexer_4 (
    .sel(ALUSrc), .in_0(registerfile_1_db), .in_1(extend_1_s), .out(multiplexer_4_out));
  Add #(.Bits(32)) add_2 (.a(PC), .b(extend_1_s), .c_i(1'b0), .s(PC_plus_0));  // open: c_o
  ULA ula_1 (.A(multiplexer_4_out), .B(rd1), .FUNC(ALUControl), .S(ALU_out), .ZERO(Zero));
  BlockRAMDualPort #(.AddrBits(7), .Bits(32)) blockramdualport_1 (
    .A(ALU_out[6:0]), .Din(registerfile_1_db), .str(MemWrite), .C(CLK), .D(blockramdualport_1_d));
  Multiplexer #(.Selector_Bits(2), .Bits(32)) multiplexer_5 (
    .sel(ResultSrc), .in_0(ALU_out), .in_1(blockramdualport_1_d), .in_2(PC_plus_4), .in_3({32{1'b0}}),
    .out(multiplexer_5_out));

  // Other names for the same wires on the sheet: I_T[31:0] = B_T; J_T[31:0] = B_T; OPCode[6:0] = B_T[6:0];
  //   S_T[31:0] = B_T; rd[4:0] = B_T[11:7]; funct3[2:0] = B_T[14:12]; rs1[4:0] = B_T[19:15]; rs2[4:0] = B_T[24:20];
  //   funct7[6:0] = B_T[31:25]

  // Notes on the sheet:
  //   CLK: Hz: 20
  //   contents of Mem__Inst (hex, n*v repeats v):
  //   1400413,0,0,0,100293,0,0,0,100313,0,0,0,8000ef,0,0,0,1,0,0,0,200493
  //   ,0,0,0,552023,0,0,0,652223,0,0,0,450513,0,0,0,6283b3,0,0,0,752223
  //   ,0,0,0,450513,0,0,0,30293,0,0,0,38313,0,0,0,148493,0,0,0,fe84c4e3
  //   ,0,0,0,80e7
endmodule
