// Digital circuit SLL.dig as structural Verilog
module SLL (
  input  [31:0] rs1,
  input  [31:0] rs2,
  output [31:0] S
);

  wire [31:0] _1, _2, _3, _4, _5, _6, _7, _8, _9, _10, _11, _12, _13, _14, _15, _16, _17, _18, _19, _20, _21,
       _22, _23, _24, _25, _26, _27, _28, _29, _30, _31;

  SLL32 sll32_1 (.rs1(rs1), .S(_1));
  SLL32 sll32_2 (.rs1(_8), .S(_9));
  SLL32 sll32_3 (.rs1(_16), .S(_17));
  SLL32 sll32_4 (.rs1(_24), .S(_25));
  SLL32 sll32_5 (.rs1(_1), .S(_2));
  SLL32 sll32_6 (.rs1(_9), .S(_10));
  SLL32 sll32_7 (.rs1(_17), .S(_18));
  SLL32 sll32_8 (.rs1(_25), .S(_26));
  SLL32 sll32_9 (.rs1(_2), .S(_3));
  SLL32 sll32_10 (.rs1(_10), .S(_11));
  SLL32 sll32_11 (.rs1(_18), .S(_19));
  SLL32 sll32_12 (.rs1(_26), .S(_27));
  SLL32 sll32_13 (.rs1(_3), .S(_4));
  SLL32 sll32_14 (.rs1(_11), .S(_12));
  SLL32 sll32_15 (.rs1(_19), .S(_20));
  SLL32 sll32_16 (.rs1(_27), .S(_28));
  SLL32 sll32_17 (.rs1(_4), .S(_5));
  SLL32 sll32_18 (.rs1(_12), .S(_13));
  SLL32 sll32_19 (.rs1(_20), .S(_21));
  SLL32 sll32_20 (.rs1(_28), .S(_29));
  SLL32 sll32_21 (.rs1(_5), .S(_6));
  SLL32 sll32_22 (.rs1(_13), .S(_14));
  SLL32 sll32_23 (.rs1(_21), .S(_22));
  SLL32 sll32_24 (.rs1(_29), .S(_30));
  SLL32 sll32_25 (.rs1(_6), .S(_7));
  SLL32 sll32_26 (.rs1(_14), .S(_15));
  SLL32 sll32_27 (.rs1(_22), .S(_23));
  SLL32 sll32_28 (.rs1(_30), .S(_31));
  SLL32 sll32_29 (.rs1(_7), .S(_8));
  SLL32 sll32_30 (.rs1(_15), .S(_16));
  SLL32 sll32_31 (.rs1(_23), .S(_24));
  Multiplexer #(.Bits(32), .Selector_Bits(5)) multiplexer_1 (
    .sel(rs2[4:0]), .in_0(rs1), .in_1(_1), .in_2(_2), .in_3(_3), .in_4(_4), .in_5(_5), .in_6(_6), .in_7(_7),
    .in_8(_8), .in_9(_9), .in_10(_10), .in_11(_11), .in_12(_12), .in_13(_13), .in_14(_14), .in_15(_15),
    .in_16(_16), .in_17(_17), .in_18(_18), .in_19(_19), .in_20(_20), .in_21(_21), .in_22(_22), .in_23(_23),
    .in_24(_24), .in_25(_25), .in_26(_26), .in_27(_27), .in_28(_28), .in_29(_29), .in_30(_30), .in_31(_31),
    .out(S));

  // Other names for the same wires on the sheet: _0[31:0] = rs1
endmodule
