// Digital circuit SLL16.dig as structural Verilog
module SLL16 (
  input  [15:0] rs1,
  input  Menos,
  input  F,
  output [15:0] S,
  output Mais
);

  Multiplexer multiplexer_1 (.sel(F), .in_0(rs1[15]), .in_1(rs1[14]), .out(Mais));
  Multiplexer multiplexer_2 (.sel(F), .in_0(rs1[14]), .in_1(rs1[13]), .out(S[14]));
  Multiplexer multiplexer_3 (.sel(F), .in_0(rs1[13]), .in_1(rs1[12]), .out(S[13]));
  Multiplexer multiplexer_4 (.sel(F), .in_0(rs1[12]), .in_1(rs1[11]), .out(S[12]));
  Multiplexer multiplexer_5 (.sel(F), .in_0(rs1[11]), .in_1(rs1[10]), .out(S[11]));
  Multiplexer multiplexer_6 (.sel(F), .in_0(rs1[10]), .in_1(rs1[9]), .out(S[10]));
  Multiplexer multiplexer_7 (.sel(F), .in_0(rs1[9]), .in_1(rs1[8]), .out(S[9]));
  Multiplexer multiplexer_8 (.sel(F), .in_0(rs1[8]), .in_1(rs1[7]), .out(S[8]));
  Multiplexer multiplexer_9 (.sel(F), .in_0(rs1[7]), .in_1(rs1[6]), .out(S[7]));
  Multiplexer multiplexer_10 (.sel(F), .in_0(rs1[6]), .in_1(rs1[5]), .out(S[6]));
  Multiplexer multiplexer_11 (.sel(F), .in_0(rs1[5]), .in_1(rs1[4]), .out(S[5]));
  Multiplexer multiplexer_12 (.sel(F), .in_0(rs1[4]), .in_1(rs1[3]), .out(S[4]));
  Multiplexer multiplexer_13 (.sel(F), .in_0(rs1[3]), .in_1(rs1[2]), .out(S[3]));
  Multiplexer multiplexer_14 (.sel(F), .in_0(rs1[2]), .in_1(rs1[1]), .out(S[2]));
  Multiplexer multiplexer_15 (.sel(F), .in_0(rs1[1]), .in_1(rs1[0]), .out(S[1]));
  Multiplexer multiplexer_16 (.sel(F), .in_0(rs1[0]), .in_1(Menos), .out(S[0]));

  assign S[15] = Mais;
endmodule
