// Digital circuit SLL32.dig as structural Verilog
module SLL32 (
  input  [31:0] rs1,
  output [31:0] S
);

  wire sll16_2_mais;

  SLL16 sll16_1 (.rs1(rs1[31:16]), .Menos(sll16_2_mais), .F(1'b1), .S(S[31:16]));  // open: Mais
  SLL16 sll16_2 (.rs1(rs1[15:0]), .Menos(1'b0), .F(1'b1), .S(S[15:0]), .Mais(sll16_2_mais));
endmodule
