// Digital circuit Sub16.dig as structural Verilog
module Sub16 (
  input  [15:0] A,
  input  [15:0] B,
  input  Cin,
  output Cout,
  output [15:0] S
);

  wire sub4_1_cout, sub4_2_cout, sub4_3_cout;

  Sub4 sub4_1 (.Cin(Cin), .B(B[3:0]), .A(A[3:0]), .S(S[3:0]), .Cout(sub4_1_cout));
  Sub4 sub4_2 (.Cin(sub4_1_cout), .B(B[7:4]), .A(A[7:4]), .S(S[7:4]), .Cout(sub4_2_cout));
  Sub4 sub4_3 (.Cin(sub4_2_cout), .B(B[11:8]), .A(A[11:8]), .S(S[11:8]), .Cout(sub4_3_cout));
  Sub4 sub4_4 (.Cin(sub4_3_cout), .B(B[15:12]), .A(A[15:12]), .S(S[15:12]), .Cout(Cout));
endmodule
