// Digital circuit Sub32.dig as structural Verilog
module Sub32 (
  input  [31:0] rs2,
  input  [31:0] rs1,
  input  Cin,
  output [31:0] S,
  output Cout
);

  wire sub16_1_cout;

  Sub16 sub16_1 (.A(rs1[15:0]), .B(rs2[15:0]), .Cin(Cin), .Cout(sub16_1_cout), .S(S[15:0]));
  Sub16 sub16_2 (.A(rs1[31:16]), .B(rs2[31:16]), .Cin(sub16_1_cout), .Cout(Cout), .S(S[31:16]));
endmodule
