// Digital circuit Sub4.dig as structural Verilog
module Sub4 (
  input  Cin,
  input  [3:0] B,
  input  [3:0] A,
  output [3:0] S,
  output Cout
);

  wire fa1_1_cout, fa1_2_cout, fa1_3_cout, not_1_out, not_2_out, not_3_out, not_4_out;

  not not_1 (not_1_out, B[0]);
  not not_2 (not_2_out, B[1]);
  not not_3 (not_3_out, B[2]);
  not not_4 (not_4_out, B[3]);
  FA1 fa1_1 (.A(A[0]), .B(not_1_out), .Cin(Cin), .Cout(fa1_1_cout), .S(S[0]));
  FA1 fa1_2 (.A(A[1]), .B(not_2_out), .Cin(fa1_1_cout), .Cout(fa1_2_cout), .S(S[1]));
  FA1 fa1_3 (.A(A[2]), .B(not_3_out), .Cin(fa1_2_cout), .Cout(fa1_3_cout), .S(S[2]));
  FA1 fa1_4 (.A(A[3]), .B(not_4_out), .Cin(fa1_3_cout), .Cout(Cout), .S(S[3]));
endmodule
