// Digital circuit ULA.dig as structural Verilog
module ULA (
  input  [31:0] A,
  input  [31:0] B,
  input  [2:0] FUNC,
  output [31:0] S,
  output ZERO
);

  wire [31:0] and_1_out, barrelshifter_1_out, fa32_1_s, not_1_out, or_1_out, sub32_1_s, xor_1_out;

  FA32 fa32_1 (.rs2(B), .rs1(A), .Cin(1'b0), .S(fa32_1_s));  // open: Cout
  Sub32 sub32_1 (.B(B), .A(A), .Cin(1'b1), .S(sub32_1_s));  // open: Cout
  assign xor_1_out = B ^ A;  // XOr xor_1, 32 bits wide
  assign or_1_out = B | A;  // Or or_1, 32 bits wide
  assign and_1_out = B & A;  // And and_1, 32 bits wide
  assign not_1_out = ~A;  // Not not_1, 32 bits wide
  BarrelShifter #(.Bits(6)) barrelshifter_1 (.in(A[5:0]), .shift(B), .out(barrelshifter_1_out[5:0]));
  Multiplexer #(.Selector_Bits(3), .Bits(32)) multiplexer_1 (
    .sel(FUNC), .in_0(fa32_1_s), .in_1(sub32_1_s), .in_2(xor_1_out), .in_3(or_1_out), .in_4(and_1_out),
    .in_5(not_1_out), .in_6(barrelshifter_1_out), .in_7(barrelshifter_1_out), .out(S));
  ZERO zero_1 (.Cin(S), .S(ZERO));
  // Pins of 6 and 32 bits meet at barrelshifter_1_out
  // Pins of 6 and 32 bits meet at A
endmodule
