// Digital circuit ZERO7.dig as structural Verilog
module ZERO7 (
  input  [4:0] OP,
  output S
);

  wire [4:0] not_1_out;

  assign not_1_out = ~OP;  // Not not_1, 5 bits wide
  and and_1 (S, not_1_out[0], not_1_out[1], not_1_out[2], not_1_out[3], not_1_out[4]);
endmodule
